// Logisim project project.circ as structural Verilog: 34 circuits, main circuit main
module main (
  output [3:0] Seq
);

  wire ac_alu_controller_1_clr, ac_alu_controller_1_inc, ar_controler_1_clr, ar_controler_1_inr,
       ar_controler_1_ld, bus_controler_1_s0, bus_controler_1_s1, bus_controler_1_s2, CLK,
       dr_controller_1_inc, dr_controller_1_ld, E, E_out, FGI, FGO, I, IEN, ir_controller_1_ld, or_1_out,
       outr_controller_1_ld, pc_controller_1_clr, pc_controller_1_inc, pc_controller_1_ld, R,
       ram_controller_1_read, ram_controller_1_write, S, sc_controller_1_inc, sc_controller_1_ld,
       tr_controller_1_ld;
  wire [6:0] ac_alu_controller_1_and;
  wire [7:0] outr_1_bus_out, undriven;
  wire [11:0] ar_1_bus_out;
  wire [15:0] AC, alu_1_out, bus_1_out_11, DR, IR, pc_1_bus_out, ram_1_data, Seq_t, tr_1_bus_out;
  wire [15:12] ar_1_bus_out_2;

  Clock u_CLK (.out(CLK));
  I_Controller i_controller_1 (.IR(IR), .R(R), .out_5(I), .Seq(Seq_t), .CLK(CLK));
  FGI_Controller fgi_controller_1 (.IR(IR), .I(I), .Seq(Seq_t), .Output(FGI), .in_3(CLK));
  FGO_Controller fgo_controller_1 (.IR(IR), .I(I), .Output(FGO), .Seq(Seq_t), .CLK(CLK));
  E_Controller e_controller_1 (.IR(IR), .R(R), .Seq(Seq_t), .Cout(E_out), .I(I), .AC(AC), .in_6(CLK), .Output(E));
  R_Controller r_controller_1 (.IEN(IEN), .FGI(FGI), .FGO(FGI), .CLK(CLK), .Output(R), .Seq(Seq_t));
  S_Controller s_controller_1 (.IR(IR), .I(I), .R(R), .Output(S), .Seq(Seq_t), .CLK(CLK));
  IEN_Controler ien_controler_1 (.IR(IR), .I(I), .R(R), .Seq(Seq_t), .CLK(CLK), .Output(IEN));
  SC_Controller sc_controller_1 (
    .IR(IR), .I(I), .R(R), .S(S), .LD(sc_controller_1_ld), .INC(sc_controller_1_inc), .Seq(Seq_t));
  Counter #(.width(4), .max('hf)) counter_1 (
    .load(sc_controller_1_ld), .D(4'b0000), .count(sc_controller_1_inc), .Q(Seq), .clk(CLK));  // open: carry, clr
  Decoder #(.select(4)) decoder_1 (
    .out0(Seq_t[0]), .out1(Seq_t[1]), .out2(Seq_t[2]), .out3(Seq_t[3]), .out4(Seq_t[4]), .out5(Seq_t[5]),
    .out6(Seq_t[6]), .out7(Seq_t[7]), .out8(Seq_t[8]), .out9(Seq_t[9]), .out10(Seq_t[10]), .out11(Seq_t[11]),
    .out12(Seq_t[12]), .out13(Seq_t[13]), .out14(Seq_t[14]), .out15(Seq_t[15]), .sel(Seq));  // open: en
  AC_ALU_Controller ac_alu_controller_1 (
    .IR(IR), .I(I), .AND(ac_alu_controller_1_and[0]), .ADD(ac_alu_controller_1_and[1]),
    .DR(ac_alu_controller_1_and[2]), .INPR(ac_alu_controller_1_and[3]), .COM(ac_alu_controller_1_and[4]),
    .SHR(ac_alu_controller_1_and[5]), .SHL(ac_alu_controller_1_and[6]), .INC(ac_alu_controller_1_inc),
    .CLR(ac_alu_controller_1_clr), .Seq(Seq_t));
  ALU alu_1 (
    .DR(DR), .AC(AC), .E_out(E_out), .INPUT(undriven), .E(E), .Out(alu_1_out),
    .AND(ac_alu_controller_1_and[0]), .ADD(ac_alu_controller_1_and[1]), .DR_2(ac_alu_controller_1_and[2]),
    .INPR(ac_alu_controller_1_and[3]), .COM(ac_alu_controller_1_and[4]), .SHR(ac_alu_controller_1_and[5]),
    .SHL(ac_alu_controller_1_and[6]));
  OUTR_Controller outr_controller_1 (.IR(IR), .I(I), .R(R), .LD(outr_controller_1_ld), .Seq(Seq_t));
  RAM #(.addrWidth(12), .dataWidth(16), .bus("separate")) ram_1 (
    .addr(ar_1_bus_out), .din(bus_1_out_11), .data(ram_1_data), .str(ram_controller_1_write), .clk(CLK),
    .ld(ram_controller_1_read));  // open: sel, clr
  RAM_Controller ram_controller_1 (
    .IR(IR), .I(I), .R(R), .Read(ram_controller_1_read), .Write(ram_controller_1_write), .Seq(Seq_t));
  AR_Controler ar_controler_1 (
    .IR(IR), .I(I), .R(R), .LD(ar_controler_1_ld), .INR(ar_controler_1_inr), .CLR(ar_controler_1_clr),
    .Seq(Seq_t));
  PC_Controller pc_controller_1 (
    .IR(IR), .I(I), .R(R), .E(E), .FGI(FGI), .FGO(FGO), .AC(AC), .DR(DR), .LD(pc_controller_1_ld),
    .INC(pc_controller_1_inc), .CLR(pc_controller_1_clr), .Seq(Seq_t));
  DR_Controller dr_controller_1 (
    .IR(IR), .I(I), .R(R), .LD(dr_controller_1_ld), .INC(dr_controller_1_inc), .Seq(Seq_t));
  or or_1 (or_1_out, ac_alu_controller_1_and[0], ac_alu_controller_1_and[1], ac_alu_controller_1_and[2], ac_alu_controller_1_and[3], ac_alu_controller_1_and[4], ac_alu_controller_1_and[5], ac_alu_controller_1_and[6]);
  IR_Controller ir_controller_1 (.IR(IR), .R(R), .LD(ir_controller_1_ld), .Seq(Seq_t));
  TR_Controller tr_controller_1 (.IR(IR), .R(R), .LD(tr_controller_1_ld), .Seq(Seq_t));
  BUS_Controler bus_controler_1 (
    .IR(IR), .R(R), .I(I), .S0(bus_controler_1_s0), .S1(bus_controler_1_s1), .S2(bus_controler_1_s2),
    .Seq(Seq_t));
  // Probe on ram_1_data
  AR ar_1 (
    .Bus_IN(bus_1_out_11), .Bus_OUT({ar_1_bus_out_2, ar_1_bus_out}), .Inc(ar_controler_1_inr),
    .Load(ar_controler_1_ld), .Clock(CLK), .Clear(ar_controler_1_clr));
  PC pc_1 (
    .Bus_OUT(pc_1_bus_out), .Bus_IN(bus_1_out_11), .Inc(pc_controller_1_inc), .Load(pc_controller_1_ld),
    .Clock(CLK), .Clear(pc_controller_1_clr));
  DR dr_1 (
    .ALU_In(bus_1_out_11), .Bus_OUT(DR), .Load(dr_controller_1_ld), .Inc(dr_controller_1_inc), .Clock(CLK));  // open: Clear
  AC ac_1 (
    .ALU_In(alu_1_out), .Bus_OUT(AC), .Inc(ac_alu_controller_1_inc), .Load(or_1_out), .Clock(CLK),
    .Clear(ac_alu_controller_1_clr));
  IR ir_1 (.BUS_IN(bus_1_out_11), .Bus_OUT(IR), .Load(ir_controller_1_ld), .Clock(CLK));
  TR tr_1 (.ALU_In(bus_1_out_11), .Bus_OUT(tr_1_bus_out), .Load(tr_controller_1_ld), .Clock(CLK));  // open: Clear
  OUTR outr_1 (.ALU_In(bus_1_out_11), .Bus_OUT(outr_1_bus_out), .Load(outr_controller_1_ld), .Clock(CLK));
  BUS bus_1 (
    .S0(bus_controler_1_s0), .S1(bus_controler_1_s1), .S2(bus_controler_1_s2),
    .AR({ar_1_bus_out_2, ar_1_bus_out}), .PC(pc_1_bus_out), .DR(DR), .AC(AC), .IR(IR), .TR(tr_1_bus_out),
    .RAM(ram_1_data), .out_11(bus_1_out_11));
  // Probe on {ar_1_bus_out_2, ar_1_bus_out}
  // Probe on pc_1_bus_out
  // Probe on DR
  // Probe on AC
  // Probe on IR
  // Probe on tr_1_bus_out
  Hex_Digit_Display hex_digit_display_1 (.value(outr_1_bus_out[7:4]));  // open: dp
  Hex_Digit_Display hex_digit_display_2 (.value(outr_1_bus_out[3:0]));  // open: dp
  // Probe on bus_1_out_11
endmodule

module BUS (
  input  S0,
  input  S1,
  input  S2,
  input  [15:0] AR,
  input  [15:0] PC,
  input  [15:0] DR,
  input  [15:0] AC,
  input  [15:0] IR,
  input  [15:0] TR,
  input  [15:0] RAM,
  output [15:0] out_11
);

  Multiplexer #(.select(3), .width(16)) multiplexer_1 (
    .in1(AR), .in2(PC), .in3(DR), .in4(AC), .in5(IR), .in6(TR), .in7(RAM), .out(out_11), .sel({S2, S1, S0}));  // open: in0, en

  // Other names for the same wires on the sheet: Selector[2:0] = {S2, S1, S0}
endmodule

module BUS_Controler (
  input  [15:0] IR,
  input  [15:0] Seq,
  input  R,
  input  I,
  output S0,
  output S1,
  output S2
);

  wire and_1_out, and_2_out, and_3_out, and_4_out, and_5_out, and_6_out, and_7_out, and_8_out, and_9_out,
       and_10_out, and_11_out, and_12_out, and_13_out, and_14_out, or_1_out, or_2_out, or_3_out, or_4_out,
       or_5_out, or_6_out;
  wire [7:0] decoder_1_out7;

  Decoder #(.select(3)) decoder_1 (
    .out0(decoder_1_out7[7]), .out1(decoder_1_out7[6]), .out2(decoder_1_out7[5]), .out3(decoder_1_out7[4]),
    .out4(decoder_1_out7[3]), .out5(decoder_1_out7[2]), .out6(decoder_1_out7[1]), .out7(decoder_1_out7[0]),
    .sel(IR[14:12]));  // open: en
  and and_1 (and_1_out, decoder_1_out7[0], Seq[3], I);
  or or_1 (or_1_out, decoder_1_out7[7], decoder_1_out7[6], decoder_1_out7[5], decoder_1_out7[1]);
  and and_2 (and_2_out, Seq[4], decoder_1_out7[3]);
  and and_3 (and_3_out, decoder_1_out7[2], Seq[5]);
  and and_4 (and_4_out, decoder_1_out7[2], Seq[4]);
  and and_5 (and_5_out, decoder_1_out7[5], Seq[5]);
  and and_6 (and_6_out, decoder_1_out7[1], Seq[6]);
  and and_7 (and_7_out, Seq[4], decoder_1_out7[4]);
  and and_8 (and_8_out, IR[10], and_1_out);
  and and_9 (and_9_out, ~R, Seq[1]);  // AND_Gate
  and and_10 (and_10_out, ~decoder_1_out7[0], I, Seq[3]);  // AND_Gate
  and and_11 (and_11_out, Seq[4], or_1_out);
  or or_2 (or_2_out, and_2_out, and_3_out);
  or or_3 (or_3_out, Seq[0], and_4_out);
  or or_4 (or_4_out, and_5_out, and_6_out);
  or or_5 (or_5_out, and_7_out, and_8_out);
  and and_12 (and_12_out, Seq[2], ~R);  // AND_Gate
  and and_13 (and_13_out, R, Seq[1]);
  or or_6 (or_6_out, and_9_out, and_10_out, and_11_out);
  and and_14 (and_14_out, ~or_6_out, ~and_13_out, ~and_12_out, ~or_5_out, ~or_4_out, ~or_3_out, ~or_2_out);  // AND_Gate
  Priority_Encoder priority_encoder_1 (
    .in0(and_14_out), .in1(or_2_out), .in2(or_3_out), .in3(or_4_out), .in4(or_5_out), .in5(and_12_out),
    .in6(and_13_out), .in7(or_6_out), .out({S2, S1, S0}));  // open: en_in, gs, en_out
endmodule

module AR (
  input  [15:0] Bus_IN,
  input  Load,
  input  Inc,
  input  Clear,
  input  Clock,
  output [15:0] Bus_OUT
);

  Counter #(.width(12), .max('hfff)) counter_1 (
    .load(Load), .D(Bus_IN[11:0]), .count(Inc), .Q(Bus_OUT[11:0]), .clk(Clock), .clr(Clear));  // open: carry

  assign Bus_OUT[15:12] = 4'b0000;
endmodule

module PC (
  input  [15:0] Bus_IN,
  input  Load,
  input  Inc,
  input  Clear,
  input  Clock,
  output [15:0] Bus_OUT
);

  Counter #(.width(12), .max('hfff)) counter_1 (
    .load(Load), .D(Bus_IN[11:0]), .count(Inc), .Q(Bus_OUT[11:0]), .clk(Clock), .clr(Clear));  // open: carry

  assign Bus_OUT[15:12] = 4'b0000;
endmodule

module DR (
  input  [15:0] ALU_In,
  input  Load,
  input  Inc,
  input  Clear,
  input  Clock,
  output [15:0] Bus_OUT
);

  Counter #(.width(16), .max('hffff)) counter_1 (
    .load(Load), .D(ALU_In), .count(Inc), .Q(Bus_OUT), .clk(Clock), .clr(Clear));  // open: carry
endmodule

module AC (
  input  [15:0] ALU_In,
  input  Load,
  input  Inc,
  input  Clock,
  input  Clear,
  output [15:0] Bus_OUT
);

  Counter #(.width(16), .max('hffff)) counter_1 (
    .load(Load), .D(ALU_In), .count(Inc), .Q(Bus_OUT), .clk(Clock), .clr(Clear));  // open: carry
endmodule

module IR (
  input  [15:0] BUS_IN,
  input  Load,
  input  Clock,
  output [15:0] Bus_OUT
);

  Counter #(.width(16), .max('hffff)) counter_1 (
    .load(Load), .D(BUS_IN), .count(1'b0), .Q(Bus_OUT), .clk(Clock), .clr(1'b0));  // open: carry
endmodule

module TR (
  input  [15:0] ALU_In,
  input  Load,
  input  Clear,
  input  Clock,
  output [15:0] Bus_OUT
);

  Counter #(.width(16), .max('hffff)) counter_1 (
    .load(Load), .D(ALU_In), .count(1'b0), .Q(Bus_OUT), .clk(Clock), .clr(Clear));  // open: carry
endmodule

module OUTR (
  input  [15:0] ALU_In,
  input  Load,
  input  Clock,
  output [7:0] Bus_OUT
);

  Counter counter_1 (.load(Load), .D(ALU_In[7:0]), .count(1'b0), .Q(Bus_OUT), .clk(Clock));  // open: carry, clr
endmodule

module ALU_1bit (
  input  DR_i,
  input  AC_i,
  input  AND,
  input  Ci,
  input  ADD,
  input  DR,
  input  INPR,
  input  INPR_i,
  input  COM,
  input  SHR,
  input  AC_i_1,
  input  SHL,
  input  AC_i_1_2,
  output C_i_1,
  output AC_i_2
);

  wire and_1_out, and_2_out, and_3_out, and_4_out, and_5_out, and_6_out, and_7_out, fa_1_s, not_1_out;

  FA fa_1 (.Cin(Ci), .A(AC_i), .B(DR_i), .S(fa_1_s), .Cout(C_i_1));
  not not_1 (not_1_out, AC_i);
  and and_1 (and_1_out, AND, AC_i, DR_i);
  and and_2 (and_2_out, fa_1_s, ADD);
  and and_3 (and_3_out, DR, DR_i);
  and and_4 (and_4_out, INPR, INPR_i);
  and and_5 (and_5_out, COM, not_1_out);
  and and_6 (and_6_out, SHR, AC_i_1);
  and and_7 (and_7_out, SHL, AC_i_1_2);
  or or_1 (AC_i_2, and_1_out, and_2_out, and_3_out, and_4_out, and_5_out, and_6_out, and_7_out);
endmodule

module ALU (
  input  [15:0] DR,
  input  [15:0] AC,
  input  [7:0] INPUT,
  input  E,
  input  AND,
  input  ADD,
  input  DR_2,
  input  INPR,
  input  COM,
  input  SHR,
  input  SHL,
  output [15:0] Out,
  output E_out
);

  wire alu_1bit_1_c_i_1, alu_1bit_2_c_i_1, alu_1bit_3_c_i_1, alu_1bit_4_c_i_1, alu_1bit_5_c_i_1,
       alu_1bit_6_c_i_1, alu_1bit_7_c_i_1, alu_1bit_8_c_i_1, alu_1bit_9_c_i_1, alu_1bit_10_c_i_1,
       alu_1bit_11_c_i_1, alu_1bit_12_c_i_1, alu_1bit_13_c_i_1, alu_1bit_14_c_i_1, alu_1bit_15_c_i_1;

  ALU_1bit alu_1bit_1 (
    .AND(AND), .ADD(ADD), .DR(DR_2), .INPR(INPR), .COM(COM), .SHR(SHR), .AC_i_1(AC[1]), .SHL(SHL),
    .AC_i_1_2(E), .AC_i_2(Out[0]), .DR_i(DR[0]), .AC_i(AC[0]), .Ci(1'b0), .C_i_1(alu_1bit_1_c_i_1));  // open: INPR_i
  ALU_1bit alu_1bit_2 (
    .AND(AND), .ADD(ADD), .DR(DR_2), .INPR(INPR), .COM(COM), .SHR(SHR), .AC_i_1(AC[2]), .SHL(SHL),
    .AC_i_1_2(AC[0]), .AC_i_2(Out[1]), .DR_i(DR[1]), .AC_i(AC[1]), .Ci(alu_1bit_1_c_i_1),
    .C_i_1(alu_1bit_2_c_i_1));  // open: INPR_i
  ALU_1bit alu_1bit_3 (
    .AND(AND), .ADD(ADD), .DR(DR_2), .INPR(INPR), .COM(COM), .SHR(SHR), .AC_i_1(AC[3]), .SHL(SHL),
    .AC_i_1_2(AC[1]), .AC_i_2(Out[2]), .DR_i(DR[2]), .AC_i(AC[2]), .Ci(alu_1bit_2_c_i_1),
    .C_i_1(alu_1bit_3_c_i_1));  // open: INPR_i
  ALU_1bit alu_1bit_4 (
    .AND(AND), .ADD(ADD), .DR(DR_2), .INPR(INPR), .COM(COM), .SHR(SHR), .AC_i_1(AC[4]), .SHL(SHL),
    .AC_i_1_2(AC[2]), .AC_i_2(Out[3]), .DR_i(DR[3]), .AC_i(AC[3]), .Ci(alu_1bit_3_c_i_1),
    .C_i_1(alu_1bit_4_c_i_1));  // open: INPR_i
  ALU_1bit alu_1bit_5 (
    .AND(AND), .ADD(ADD), .DR(DR_2), .INPR(INPR), .COM(COM), .SHR(SHR), .AC_i_1(AC[5]), .SHL(SHL),
    .AC_i_1_2(AC[3]), .AC_i_2(Out[4]), .DR_i(DR[4]), .AC_i(AC[4]), .Ci(alu_1bit_4_c_i_1),
    .C_i_1(alu_1bit_5_c_i_1));  // open: INPR_i
  ALU_1bit alu_1bit_6 (
    .AND(AND), .ADD(ADD), .DR(DR_2), .INPR(INPR), .COM(COM), .SHR(SHR), .AC_i_1(AC[6]), .SHL(SHL),
    .AC_i_1_2(AC[4]), .AC_i_2(Out[5]), .DR_i(DR[5]), .AC_i(AC[5]), .Ci(alu_1bit_5_c_i_1),
    .C_i_1(alu_1bit_6_c_i_1));  // open: INPR_i
  ALU_1bit alu_1bit_7 (
    .AND(AND), .ADD(ADD), .DR(DR_2), .INPR(INPR), .COM(COM), .SHR(SHR), .AC_i_1(AC[7]), .SHL(SHL),
    .AC_i_1_2(AC[5]), .AC_i_2(Out[6]), .DR_i(DR[6]), .AC_i(AC[6]), .Ci(alu_1bit_6_c_i_1),
    .C_i_1(alu_1bit_7_c_i_1));  // open: INPR_i
  ALU_1bit alu_1bit_8 (
    .AND(AND), .ADD(ADD), .DR(DR_2), .INPR(INPR), .COM(COM), .SHR(SHR), .AC_i_1(AC[8]), .SHL(SHL),
    .AC_i_1_2(AC[6]), .AC_i_2(Out[7]), .DR_i(DR[7]), .AC_i(AC[7]), .Ci(alu_1bit_7_c_i_1),
    .C_i_1(alu_1bit_8_c_i_1));  // open: INPR_i
  ALU_1bit alu_1bit_9 (
    .AND(AND), .ADD(ADD), .DR(DR_2), .INPR(INPR), .COM(COM), .SHR(SHR), .AC_i_1(AC[9]), .SHL(SHL),
    .AC_i_1_2(AC[7]), .AC_i_2(Out[8]), .DR_i(DR[8]), .AC_i(AC[8]), .Ci(alu_1bit_8_c_i_1),
    .C_i_1(alu_1bit_9_c_i_1));  // open: INPR_i
  ALU_1bit alu_1bit_10 (
    .AND(AND), .ADD(ADD), .DR(DR_2), .INPR(INPR), .COM(COM), .SHR(SHR), .AC_i_1(AC[10]), .SHL(SHL),
    .AC_i_1_2(AC[8]), .AC_i_2(Out[9]), .DR_i(DR[9]), .AC_i(AC[9]), .Ci(alu_1bit_9_c_i_1),
    .C_i_1(alu_1bit_10_c_i_1));  // open: INPR_i
  ALU_1bit alu_1bit_11 (
    .AND(AND), .ADD(ADD), .DR(DR_2), .INPR(INPR), .COM(COM), .SHR(SHR), .AC_i_1(AC[11]), .SHL(SHL),
    .AC_i_1_2(AC[9]), .AC_i_2(Out[10]), .DR_i(DR[10]), .AC_i(AC[10]), .Ci(alu_1bit_10_c_i_1),
    .C_i_1(alu_1bit_11_c_i_1));  // open: INPR_i
  ALU_1bit alu_1bit_12 (
    .AND(AND), .ADD(ADD), .DR(DR_2), .INPR(INPR), .COM(COM), .SHR(SHR), .AC_i_1(AC[12]), .SHL(SHL),
    .AC_i_1_2(AC[10]), .AC_i_2(Out[11]), .DR_i(DR[11]), .AC_i(AC[11]), .Ci(alu_1bit_11_c_i_1),
    .C_i_1(alu_1bit_12_c_i_1));  // open: INPR_i
  ALU_1bit alu_1bit_13 (
    .AND(AND), .ADD(ADD), .DR(DR_2), .INPR(INPR), .COM(COM), .SHR(SHR), .AC_i_1(AC[13]), .SHL(SHL),
    .AC_i_1_2(AC[11]), .AC_i_2(Out[12]), .DR_i(DR[12]), .AC_i(AC[12]), .Ci(alu_1bit_12_c_i_1),
    .C_i_1(alu_1bit_13_c_i_1));  // open: INPR_i
  ALU_1bit alu_1bit_14 (
    .AND(AND), .ADD(ADD), .DR(DR_2), .INPR(INPR), .COM(COM), .SHR(SHR), .AC_i_1(AC[14]), .SHL(SHL),
    .AC_i_1_2(AC[12]), .AC_i_2(Out[13]), .DR_i(DR[13]), .AC_i(AC[13]), .Ci(alu_1bit_13_c_i_1),
    .C_i_1(alu_1bit_14_c_i_1));  // open: INPR_i
  ALU_1bit alu_1bit_15 (
    .AND(AND), .ADD(ADD), .DR(DR_2), .INPR(INPR), .COM(COM), .SHR(SHR), .AC_i_1(AC[15]), .SHL(SHL),
    .AC_i_1_2(AC[13]), .AC_i_2(Out[14]), .DR_i(DR[14]), .AC_i(AC[14]), .Ci(alu_1bit_14_c_i_1),
    .C_i_1(alu_1bit_15_c_i_1));  // open: INPR_i
  ALU_1bit alu_1bit_16 (
    .AND(AND), .ADD(ADD), .DR(DR_2), .INPR(INPR), .COM(COM), .SHR(SHR), .AC_i_1(E), .SHL(SHL),
    .AC_i_1_2(AC[14]), .AC_i_2(Out[15]), .DR_i(DR[15]), .AC_i(AC[15]), .Ci(alu_1bit_15_c_i_1), .C_i_1(E_out));  // open: INPR_i

  // Other names for the same wires on the sheet: DR_t = DR_2
endmodule

module FA (
  input  Cin,
  input  A,
  input  B,
  output S,
  output Cout
);

  wire and_1_out, and_2_out, xor_1_out;

  xor xor_1 (xor_1_out, A, B);
  and and_1 (and_1_out, A, B);
  xor xor_2 (S, xor_1_out, Cin);
  and and_2 (and_2_out, xor_1_out, Cin);
  or or_1 (Cout, and_2_out, and_1_out);
endmodule

module _12_bit_adder (
  input  Cin,
  input  [11:0] in_2,
  input  [11:0] in_3,
  output [11:0] out_4,
  output out_5
);

  wire buffer_1_out, fa_1_cout, fa_2_cout, fa_3_cout, fa_4_cout, fa_5_cout, fa_6_cout, fa_7_cout, fa_8_cout,
       fa_9_cout, fa_10_cout, fa_11_cout;

  buf buffer_1 (buffer_1_out, Cin);
  FA fa_1 (.Cin(buffer_1_out), .A(in_2[0]), .B(in_3[0]), .S(out_4[0]), .Cout(fa_1_cout));
  FA fa_2 (.Cin(fa_1_cout), .A(in_2[1]), .B(in_3[1]), .S(out_4[1]), .Cout(fa_2_cout));
  FA fa_3 (.Cin(fa_2_cout), .A(in_2[2]), .B(in_3[2]), .S(out_4[2]), .Cout(fa_3_cout));
  FA fa_4 (.Cin(fa_3_cout), .A(in_2[3]), .B(in_3[3]), .S(out_4[3]), .Cout(fa_4_cout));
  FA fa_5 (.Cin(fa_4_cout), .A(in_2[4]), .B(in_3[4]), .S(out_4[4]), .Cout(fa_5_cout));
  FA fa_6 (.Cin(fa_5_cout), .A(in_2[5]), .B(in_3[5]), .S(out_4[5]), .Cout(fa_6_cout));
  FA fa_7 (.Cin(fa_6_cout), .A(in_2[6]), .B(in_3[6]), .S(out_4[6]), .Cout(fa_7_cout));
  FA fa_8 (.Cin(fa_7_cout), .A(in_2[7]), .B(in_3[7]), .S(out_4[7]), .Cout(fa_8_cout));
  FA fa_9 (.Cin(fa_8_cout), .A(in_2[8]), .B(in_3[8]), .S(out_4[8]), .Cout(fa_9_cout));
  FA fa_10 (.Cin(fa_9_cout), .A(in_2[9]), .B(in_3[9]), .S(out_4[9]), .Cout(fa_10_cout));
  FA fa_11 (.Cin(fa_10_cout), .A(in_2[10]), .B(in_3[10]), .S(out_4[10]), .Cout(fa_11_cout));
  FA fa_12 (.Cin(fa_11_cout), .A(in_2[11]), .B(in_3[11]), .S(out_4[11]), .Cout(out_5));

  // Other names for the same wires on the sheet: A0 = in_2[0]; A1 = in_2[1]; A2 = in_2[2]; A3 = in_2[3]; A4 = in_2[4];
  //   A5 = in_2[5]; A6 = in_2[6]; A7 = in_2[7]; A8 = in_2[8]; A9 = in_2[9]; A10 = in_2[10]; A11 = in_2[11];
  //   B0 = in_3[0]; B1 = in_3[1]; B2 = in_3[2]; B3 = in_3[3]; B4 = in_3[4]; B5 = in_3[5]; B6 = in_3[6]; B7 = in_3[7];
  //   B8 = in_3[8]; B9 = in_3[9]; B10 = in_3[10]; B11 = in_3[11]

  // Notes on the sheet:
  //   A
  //   B
  //   A0
  //   B0
  //   A1
  //   B1
  //   A2
  //   B2
  //   A3
  //   B3
  //   A4
  //   B4
  //   A5
  //   B5
  //   A6
  //   B6
  //   A7
  //   B7
endmodule

module _16_Bit_Adder (
  input  Cin,
  input  [15:0] in_2,
  input  [15:0] in_3,
  output [15:0] out_4,
  output out_5
);

  wire buffer_1_out, fa_1_cout, fa_2_cout, fa_3_cout, fa_4_cout, fa_5_cout, fa_6_cout, fa_7_cout, fa_8_cout,
       fa_9_cout, fa_10_cout, fa_11_cout, fa_12_cout, fa_13_cout, fa_14_cout, fa_15_cout;

  buf buffer_1 (buffer_1_out, Cin);
  FA fa_1 (.Cin(buffer_1_out), .A(in_2[0]), .B(in_3[0]), .S(out_4[0]), .Cout(fa_1_cout));
  FA fa_2 (.Cin(fa_1_cout), .A(in_2[1]), .B(in_3[1]), .S(out_4[1]), .Cout(fa_2_cout));
  FA fa_3 (.Cin(fa_2_cout), .A(in_2[2]), .B(in_3[2]), .S(out_4[2]), .Cout(fa_3_cout));
  FA fa_4 (.Cin(fa_3_cout), .A(in_2[3]), .B(in_3[3]), .S(out_4[3]), .Cout(fa_4_cout));
  FA fa_5 (.Cin(fa_4_cout), .A(in_2[4]), .B(in_3[4]), .S(out_4[4]), .Cout(fa_5_cout));
  FA fa_6 (.Cin(fa_5_cout), .A(in_2[5]), .B(in_3[5]), .S(out_4[5]), .Cout(fa_6_cout));
  FA fa_7 (.Cin(fa_6_cout), .A(in_2[6]), .B(in_3[6]), .S(out_4[6]), .Cout(fa_7_cout));
  FA fa_8 (.Cin(fa_7_cout), .A(in_2[7]), .B(in_3[7]), .S(out_4[7]), .Cout(fa_8_cout));
  FA fa_9 (.Cin(fa_8_cout), .A(in_2[8]), .B(in_3[8]), .S(out_4[8]), .Cout(fa_9_cout));
  FA fa_10 (.Cin(fa_9_cout), .A(in_2[9]), .B(in_3[9]), .S(out_4[9]), .Cout(fa_10_cout));
  FA fa_11 (.Cin(fa_10_cout), .A(in_2[10]), .B(in_3[10]), .S(out_4[10]), .Cout(fa_11_cout));
  FA fa_12 (.Cin(fa_11_cout), .A(in_2[11]), .B(in_3[11]), .S(out_4[11]), .Cout(fa_12_cout));
  FA fa_13 (.Cin(fa_12_cout), .A(in_2[12]), .B(in_3[12]), .S(out_4[12]), .Cout(fa_13_cout));
  FA fa_14 (.Cin(fa_13_cout), .A(in_2[13]), .B(in_3[13]), .S(out_4[13]), .Cout(fa_14_cout));
  FA fa_15 (.Cin(fa_14_cout), .A(in_2[14]), .B(in_3[14]), .S(out_4[14]), .Cout(fa_15_cout));
  FA fa_16 (.Cin(fa_15_cout), .A(in_2[15]), .B(in_3[15]), .S(out_4[15]), .Cout(out_5));

  // Other names for the same wires on the sheet: A0 = in_2[0]; A1 = in_2[1]; A2 = in_2[2]; A3 = in_2[3]; A4 = in_2[4];
  //   A5 = in_2[5]; A6 = in_2[6]; A7 = in_2[7]; A8 = in_2[8]; A9 = in_2[9]; A10 = in_2[10]; A11 = in_2[11];
  //   A12 = in_2[12]; A13 = in_2[13]; A14 = in_2[14]; A15 = in_2[15]; B0 = in_3[0]; B1 = in_3[1]; B2 = in_3[2];
  //   B3 = in_3[3]; B4 = in_3[4]; B5 = in_3[5]; B6 = in_3[6]; B7 = in_3[7]; B8 = in_3[8]; B9 = in_3[9];
  //   B10 = in_3[10]; B11 = in_3[11]; B12 = in_3[12]; B13 = in_3[13]; B14 = in_3[14]; B15 = in_3[15]

  // Notes on the sheet:
  //   A
  //   B
  //   A0
  //   B0
  //   A1
  //   B1
  //   A2
  //   B2
  //   A3
  //   B3
  //   A4
  //   B4
  //   A5
  //   B5
  //   A6
  //   B6
  //   A7
  //   B7
endmodule

module Shifter (
  input  in_1,
  input  [15:0] in_2,
  input  Ir,
  output [15:0] out_4
);

  Multiplexer multiplexer_1 (.in0(Ir), .in1(in_2[1]), .out(out_4[0]), .sel(in_1));  // open: en
  Multiplexer multiplexer_2 (.in0(in_2[0]), .in1(in_2[2]), .out(out_4[1]), .sel(in_1));  // open: en
  Multiplexer multiplexer_3 (.in0(in_2[1]), .in1(in_2[3]), .out(out_4[2]), .sel(in_1));  // open: en
  Multiplexer multiplexer_4 (.in0(in_2[2]), .in1(in_2[4]), .out(out_4[3]), .sel(in_1));  // open: en
  Multiplexer multiplexer_5 (.in0(in_2[3]), .in1(in_2[5]), .out(out_4[4]), .sel(in_1));  // open: en
  Multiplexer multiplexer_6 (.in0(in_2[4]), .in1(in_2[6]), .out(out_4[5]), .sel(in_1));  // open: en
  Multiplexer multiplexer_7 (.in0(in_2[5]), .in1(in_2[7]), .out(out_4[6]), .sel(in_1));  // open: en
  Multiplexer multiplexer_8 (.in0(in_2[6]), .in1(in_2[8]), .out(out_4[7]), .sel(in_1));  // open: en
  Multiplexer multiplexer_9 (.in0(in_2[7]), .in1(in_2[9]), .out(out_4[8]), .sel(in_1));  // open: en
  Multiplexer multiplexer_10 (.in0(in_2[8]), .in1(in_2[10]), .out(out_4[9]), .sel(in_1));  // open: en
  Multiplexer multiplexer_11 (.in0(in_2[9]), .in1(in_2[11]), .out(out_4[10]), .sel(in_1));  // open: en
  Multiplexer multiplexer_12 (.in0(in_2[10]), .in1(in_2[12]), .out(out_4[11]), .sel(in_1));  // open: en
  Multiplexer multiplexer_13 (.in0(in_2[11]), .in1(in_2[13]), .out(out_4[12]), .sel(in_1));  // open: en
  Multiplexer multiplexer_14 (.in0(in_2[12]), .in1(in_2[14]), .out(out_4[13]), .sel(in_1));  // open: en
  Multiplexer multiplexer_15 (.in0(in_2[13]), .in1(in_2[15]), .out(out_4[14]), .sel(in_1));  // open: en
  Multiplexer multiplexer_16 (.in0(in_2[14]), .in1(Ir), .out(out_4[15]), .sel(in_1));  // open: en

  // Other names for the same wires on the sheet: Inp = Ir; S = in_1

  // Notes on the sheet:
  //   برای شیفت به راست S=1
  //   برای شیفت به چپS=0
endmodule

module RAM_Controller (
  input  [15:0] IR,
  input  [15:0] Seq,
  input  I,
  input  R,
  output Read,
  output Write
);

  wire and_1_out, and_2_out, and_3_out, and_4_out, and_5_out, and_6_out, and_7_out, or_1_out;
  wire [7:0] decoder_1_out7;

  Decoder #(.select(3)) decoder_1 (
    .out0(decoder_1_out7[7]), .out1(decoder_1_out7[6]), .out2(decoder_1_out7[5]), .out3(decoder_1_out7[4]),
    .out4(decoder_1_out7[3]), .out5(decoder_1_out7[2]), .out6(decoder_1_out7[1]), .out7(decoder_1_out7[0]),
    .sel(IR[14:12]));  // open: en
  or or_1 (or_1_out, decoder_1_out7[7], decoder_1_out7[6], decoder_1_out7[5], decoder_1_out7[1]);
  and and_1 (and_1_out, ~R, Seq[1]);  // AND_Gate
  and and_2 (and_2_out, ~decoder_1_out7[0], I, Seq[3]);  // AND_Gate
  and and_3 (and_3_out, or_1_out, Seq[4]);
  and and_4 (and_4_out, R, Seq[1]);
  and and_5 (and_5_out, Seq[4], decoder_1_out7[4]);
  and and_6 (and_6_out, Seq[4], decoder_1_out7[2]);
  and and_7 (and_7_out, decoder_1_out7[1], Seq[6]);
  or or_2 (Write, and_4_out, and_5_out, and_6_out, and_7_out);
  or or_3 (Read, and_1_out, and_2_out, and_3_out);

  // Notes on the sheet:
  //   T
  //   B
  //   D
endmodule

module AR_Controler (
  input  [15:0] IR,
  input  [15:0] Seq,
  input  I,
  input  R,
  output LD,
  output INR,
  output CLR
);

  wire and_1_out, and_2_out, and_3_out;
  wire [7:0] decoder_1_out7;

  Decoder #(.select(3)) decoder_1 (
    .out0(decoder_1_out7[7]), .out1(decoder_1_out7[6]), .out2(decoder_1_out7[5]), .out3(decoder_1_out7[4]),
    .out4(decoder_1_out7[3]), .out5(decoder_1_out7[2]), .out6(decoder_1_out7[1]), .out7(decoder_1_out7[0]),
    .sel(IR[14:12]));  // open: en
  and and_1 (and_1_out, ~decoder_1_out7[0], I, Seq[3]);  // AND_Gate
  and and_2 (and_2_out, Seq[2], ~R);  // AND_Gate
  and and_3 (and_3_out, ~R, Seq[0]);  // AND_Gate
  and and_4 (INR, decoder_1_out7[2], Seq[4]);
  and and_5 (CLR, Seq[0], R);
  or or_1 (LD, and_1_out, and_2_out, and_3_out);
endmodule

module PC_Controller (
  input  [15:0] IR,
  input  [15:0] Seq,
  input  I,
  input  R,
  input  E,
  input  FGI,
  input  FGO,
  input  [15:0] AC,
  input  [15:0] DR,
  output LD,
  output INC,
  output CLR
);

  wire AC_t, and_2_out, and_3_out, and_4_out, and_5_out, and_6_out, and_7_out, and_8_out, and_9_out,
       and_10_out, and_11_out, and_12_out, DR_t, p_2_out, p_out, r_t;
  wire [7:0] decoder_1_out7;

  or or_1 (AC_t, AC[0], AC[1], AC[2], AC[3], AC[4], AC[5], AC[6], AC[7], AC[8], AC[9], AC[10], AC[11], AC[12], AC[13], AC[14], AC[15]);
  or or_2 (DR_t, DR[0], DR[1], DR[2], DR[3], DR[4], DR[5], DR[6], DR[7], DR[8], DR[9], DR[10], DR[11], DR[12], DR[13], DR[14], DR[15]);
  Decoder #(.select(3)) decoder_1 (
    .out0(decoder_1_out7[7]), .out1(decoder_1_out7[6]), .out2(decoder_1_out7[5]), .out3(decoder_1_out7[4]),
    .out4(decoder_1_out7[3]), .out5(decoder_1_out7[2]), .out6(decoder_1_out7[1]), .out7(decoder_1_out7[0]),
    .sel(IR[14:12]));  // open: en
  and p (p_out, decoder_1_out7[0], I, Seq[3]);
  and p_2 (p_2_out, decoder_1_out7[0], I, Seq[3]);
  and and_1 (r_t, decoder_1_out7[0], Seq[3], ~I);  // AND_Gate
  and and_2 (and_2_out, Seq[4], decoder_1_out7[3]);
  and and_3 (and_3_out, decoder_1_out7[2], Seq[5]);
  or or_3 (LD, and_2_out, and_3_out);
  and and_4 (and_4_out, ~R, Seq[1]);  // AND_Gate
  and and_5 (and_5_out, R, Seq[2]);
  and and_6 (and_6_out, r_t, IR[3], AC[15]);
  and and_7 (and_7_out, r_t, IR[4], ~AC[15]);  // AND_Gate
  and and_8 (and_8_out, r_t, IR[2], ~AC_t);  // AND_Gate
  and and_9 (and_9_out, r_t, IR[1], ~E);  // AND_Gate
  and and_10 (and_10_out, p_out, IR[9], FGI);
  and and_11 (and_11_out, p_2_out, IR[8], FGO);
  and and_12 (and_12_out, decoder_1_out7[1], Seq[6], ~DR_t);  // AND_Gate
  and and_13 (CLR, R, Seq[1]);
  or or_4 (INC, and_4_out, and_5_out, and_6_out, and_7_out, and_8_out, and_9_out, and_10_out, and_11_out, and_12_out);

  // Other names for the same wires on the sheet: AC_15 = AC[15]

  // Notes on the sheet:
  //   T
  //   B
  //   D
endmodule

module DR_Controller (
  input  [15:0] IR,
  input  [15:0] Seq,
  input  I,
  input  R,
  output LD,
  output INC
);

  wire or_1_out;
  wire [7:0] decoder_1_out7;

  Decoder #(.select(3)) decoder_1 (
    .out0(decoder_1_out7[7]), .out1(decoder_1_out7[6]), .out2(decoder_1_out7[5]), .out3(decoder_1_out7[4]),
    .out4(decoder_1_out7[3]), .out5(decoder_1_out7[2]), .out6(decoder_1_out7[1]), .out7(decoder_1_out7[0]),
    .sel(IR[14:12]));  // open: en
  or or_1 (or_1_out, decoder_1_out7[7], decoder_1_out7[6], decoder_1_out7[5], decoder_1_out7[1]);
  and and_1 (LD, or_1_out, Seq[4]);
  and and_2 (INC, Seq[5], decoder_1_out7[1]);

  // Notes on the sheet:
  //   T
  //   B
  //   D
endmodule

module AC_Controller (
  input  [15:0] IR,
  input  [15:0] Seq,
  input  I,
  input  R,
  output LD,
  output INC,
  output CLR
);

  wire ADD_out, AND_out, COM_out, DR_out, INPR_out, p_out, SHL_out, SHR_out;
  wire [7:0] decoder_1_out7;

  Decoder #(.select(3)) decoder_1 (
    .out0(decoder_1_out7[7]), .out1(decoder_1_out7[6]), .out2(decoder_1_out7[5]), .out3(decoder_1_out7[4]),
    .out4(decoder_1_out7[3]), .out5(decoder_1_out7[2]), .out6(decoder_1_out7[1]), .out7(decoder_1_out7[0]),
    .sel(IR[14:12]));  // open: en
  and p (p_out, decoder_1_out7[0], I, Seq[3]);
  and AND (AND_out, decoder_1_out7[7], Seq[5]);
  and ADD (ADD_out, decoder_1_out7[6], Seq[5]);
  and DR (DR_out, decoder_1_out7[5], Seq[5]);
  and INPR (INPR_out, p_out, IR[11]);
  and COM (COM_out, R, IR[9]);
  and SHR (SHR_out, R, IR[7]);
  and SHL (SHL_out, R, IR[6]);
  and u_INC (INC, R, IR[5]);
  and u_CLR (CLR, R, IR[11]);
  or or_1 (LD, AND_out, ADD_out, DR_out, INPR_out, COM_out, SHR_out, SHL_out);
endmodule

module AC_ALU_Controller (
  input  [15:0] IR,
  input  [15:0] Seq,
  input  I,
  output AND,
  output ADD,
  output DR,
  output INPR,
  output COM,
  output SHR,
  output SHL,
  output INC,
  output CLR
);

  wire p_out, r;
  wire [7:0] decoder_1_out7;

  Decoder #(.select(3)) decoder_1 (
    .out0(decoder_1_out7[7]), .out1(decoder_1_out7[6]), .out2(decoder_1_out7[5]), .out3(decoder_1_out7[4]),
    .out4(decoder_1_out7[3]), .out5(decoder_1_out7[2]), .out6(decoder_1_out7[1]), .out7(decoder_1_out7[0]),
    .sel(IR[14:12]));  // open: en
  and p (p_out, decoder_1_out7[0], I, Seq[3]);
  and and_1 (r, decoder_1_out7[0], Seq[3], ~I);  // AND_Gate
  and AND_2 (AND, decoder_1_out7[7], Seq[5]);
  and u_ADD (ADD, decoder_1_out7[6], Seq[5]);
  and u_DR (DR, decoder_1_out7[5], Seq[5]);
  and u_INPR (INPR, p_out, IR[11]);
  and u_COM (COM, r, IR[9]);
  and u_SHR (SHR, r, IR[7]);
  and u_SHL (SHL, r, IR[6]);
  and u_INC (INC, r, IR[5]);
  and u_CLR (CLR, r, IR[11]);
endmodule

module IR_Controller (
  input  [15:0] IR,
  input  [15:0] Seq,
  input  R,
  output LD
);

  wire [7:0] decoder_1_out7;

  Decoder #(.select(3)) decoder_1 (
    .out0(decoder_1_out7[7]), .out1(decoder_1_out7[6]), .out2(decoder_1_out7[5]), .out3(decoder_1_out7[4]),
    .out4(decoder_1_out7[3]), .out5(decoder_1_out7[2]), .out6(decoder_1_out7[1]), .out7(decoder_1_out7[0]),
    .sel(IR[14:12]));  // open: en
  and and_1 (LD, ~R, Seq[1]);  // AND_Gate

  // Notes on the sheet:
  //   T
  //   B
  //   D
endmodule

module TR_Controller (
  input  [15:0] IR,
  input  [15:0] Seq,
  input  R,
  output LD
);

  wire [7:0] decoder_1_out7;

  Decoder #(.select(3)) decoder_1 (
    .out0(decoder_1_out7[7]), .out1(decoder_1_out7[6]), .out2(decoder_1_out7[5]), .out3(decoder_1_out7[4]),
    .out4(decoder_1_out7[3]), .out5(decoder_1_out7[2]), .out6(decoder_1_out7[1]), .out7(decoder_1_out7[0]),
    .sel(IR[14:12]));  // open: en
  and and_1 (LD, R, Seq[0]);

  // Notes on the sheet:
  //   T
  //   B
  //   D
endmodule

module OUTR_Controller (
  input  [15:0] IR,
  input  [15:0] Seq,
  input  I,
  input  R,
  output LD
);

  wire p_out;
  wire [7:0] decoder_1_out7;

  Decoder #(.select(3)) decoder_1 (
    .out0(decoder_1_out7[7]), .out1(decoder_1_out7[6]), .out2(decoder_1_out7[5]), .out3(decoder_1_out7[4]),
    .out4(decoder_1_out7[3]), .out5(decoder_1_out7[2]), .out6(decoder_1_out7[1]), .out7(decoder_1_out7[0]),
    .sel(IR[14:12]));  // open: en
  and p (p_out, decoder_1_out7[0], I, Seq[3]);
  and and_1 (LD, p_out, IR[10]);

  // Notes on the sheet:
  //   T
  //   B
  //   D
endmodule

module E_Controller (
  input  [15:0] IR,
  input  [15:0] AC,
  input  [15:0] Seq,
  input  R,
  input  I,
  input  in_6,
  input  Cout,
  output Output
);

  wire and_1_out, and_2_out, and_3_out, and_4_out, D1T5Cout_out, or_1_out, or_2_out, r_2_out, r_out,
       rB6AC_15__prime_out, rB7AC_0__prime_out, rB8_out, rB10_out;
  wire [7:0] decoder_1_out7;

  Decoder #(.select(3)) decoder_1 (
    .out0(decoder_1_out7[7]), .out1(decoder_1_out7[6]), .out2(decoder_1_out7[5]), .out3(decoder_1_out7[4]),
    .out4(decoder_1_out7[3]), .out5(decoder_1_out7[2]), .out6(decoder_1_out7[1]), .out7(decoder_1_out7[0]),
    .sel(IR[14:12]));  // open: en
  and u_r (r_out, ~I, Seq[3], decoder_1_out7[0]);  // AND_Gate
  and r_2 (r_2_out, ~I, Seq[3], decoder_1_out7[0]);  // AND_Gate
  and and_1 (and_1_out, decoder_1_out7[6], Cout, Seq[5]);
  and and_2 (and_2_out, r_out, AC[15], IR[6]);
  and and_3 (and_3_out, r_out, IR[7], AC[0]);
  and and_4 (and_4_out, r_out, IR[8]);
  and rB10 (rB10_out, r_2_out, IR[10]);
  and rB8 (rB8_out, r_2_out, IR[8]);
  and D1T5Cout (D1T5Cout_out, ~Cout, decoder_1_out7[6], Seq[5]);  // AND_Gate
  and rB7AC_0__prime (rB7AC_0__prime_out, r_2_out, IR[7], ~AC[0]);  // AND_Gate
  and rB6AC_15__prime (rB6AC_15__prime_out, r_2_out, IR[6], ~AC[15]);  // AND_Gate
  or or_1 (or_1_out, and_1_out, and_2_out, and_3_out, and_4_out);
  or or_2 (or_2_out, rB10_out, rB8_out, D1T5Cout_out, rB7AC_0__prime_out, rB6AC_15__prime_out);
  J_K_Flip_Flop j_k_ff_1 (.J(or_1_out), .clk(in_6), .K(or_2_out), .Q(Output));  // open: Qn, preset, en, reset

  // Notes on the sheet:
  //   AC
  //   T
  //   B
  //   D
endmodule

module R_Controller (
  input  [15:0] Seq,
  input  IEN,
  input  FGI,
  input  FGO,
  input  CLK,
  output Output
);

  wire and_1_out, and_2_out, or_1_out;

  or or_1 (or_1_out, FGI, FGO);
  and and_1 (and_1_out, ~Seq[0], ~Seq[1], ~Seq[2], IEN, or_1_out);  // AND_Gate
  and and_2 (and_2_out, Seq[2], Output);
  J_K_Flip_Flop j_k_ff_1 (.J(and_1_out), .clk(CLK), .K(and_2_out), .Q(Output));  // open: Qn, preset, en, reset

  // Notes on the sheet:
  //   T
endmodule

module I_Controller (
  input  [15:0] IR,
  input  [15:0] Seq,
  input  CLK,
  input  R,
  output out_5
);

  wire and_1_out, and_2_out;

  and and_1 (and_1_out, Seq[2], IR[15], ~R);  // AND_Gate
  and and_2 (and_2_out, ~R, Seq[2], ~IR[15]);  // AND_Gate
  J_K_Flip_Flop j_k_ff_1 (.J(and_1_out), .clk(CLK), .K(and_2_out), .Q(out_5));  // open: Qn, preset, en, reset

  // Notes on the sheet:
  //   T
  //   B
endmodule

module S_Controller (
  input  [15:0] IR,
  input  [15:0] Seq,
  input  CLK,
  input  I,
  input  R,
  output Output
);

  wire and_1_out, and_2_out;
  wire [7:0] decoder_1_out7;

  Decoder #(.select(3)) decoder_1 (
    .out0(decoder_1_out7[7]), .out1(decoder_1_out7[6]), .out2(decoder_1_out7[5]), .out3(decoder_1_out7[4]),
    .out4(decoder_1_out7[3]), .out5(decoder_1_out7[2]), .out6(decoder_1_out7[1]), .out7(decoder_1_out7[0]),
    .sel(IR[14:12]));  // open: en
  and and_1 (and_1_out, decoder_1_out7[0], ~I, Seq[3]);  // AND_Gate
  and and_2 (and_2_out, and_1_out, IR[0]);
  J_K_Flip_Flop j_k_ff_1 (.J(1'b0), .clk(CLK), .K(1'b0), .Qn(Output), .preset(and_2_out));  // open: Q, en, reset

  // Notes on the sheet:
  //   T
  //   B
  //   D
endmodule

module IEN_Controler (
  input  [15:0] IR,
  input  [15:0] Seq,
  input  I,
  input  CLK,
  input  R,
  output Output
);

  wire and_1_out, and_3_out, and_4_out, and_5_out, or_1_out;
  wire [7:0] decoder_1_out7;

  Decoder #(.select(3)) decoder_1 (
    .out0(decoder_1_out7[7]), .out1(decoder_1_out7[6]), .out2(decoder_1_out7[5]), .out3(decoder_1_out7[4]),
    .out4(decoder_1_out7[3]), .out5(decoder_1_out7[2]), .out6(decoder_1_out7[1]), .out7(decoder_1_out7[0]),
    .sel(IR[14:12]));  // open: en
  and and_1 (and_1_out, decoder_1_out7[0], I, Seq[3]);
  and and_2 (IR[6], decoder_1_out7[0], I, Seq[3]);
  and and_3 (and_3_out, and_1_out, IR[7]);
  and and_4 (and_4_out, IR[6], IR[6]);
  and and_5 (and_5_out, R, Seq[2]);
  or or_1 (or_1_out, and_4_out, and_5_out);
  J_K_Flip_Flop j_k_ff_1 (.J(and_3_out), .clk(CLK), .K(or_1_out), .Q(Output));  // open: Qn, preset, en, reset

  // Notes on the sheet:
  //   T
  //   B
  //   D
endmodule

module FGI_Controller (
  input  [15:0] IR,
  input  [15:0] Seq,
  input  in_3,
  input  I,
  output Output
);

  wire and_1_out, p_out;
  wire [7:0] decoder_1_out7;

  Decoder #(.select(3)) decoder_1 (
    .out0(decoder_1_out7[7]), .out1(decoder_1_out7[6]), .out2(decoder_1_out7[5]), .out3(decoder_1_out7[4]),
    .out4(decoder_1_out7[3]), .out5(decoder_1_out7[2]), .out6(decoder_1_out7[1]), .out7(decoder_1_out7[0]),
    .sel(IR[14:12]));  // open: en
  and p (p_out, decoder_1_out7[0], I, Seq[3]);
  and and_1 (and_1_out, p_out, IR[11]);
  J_K_Flip_Flop j_k_ff_1 (.J(1'b0), .clk(in_3), .K(and_1_out), .Q(Output));  // open: Qn, preset, en, reset

  // Notes on the sheet:
  //   T
  //   B
  //   D
endmodule

module FGO_Controller (
  input  [15:0] IR,
  input  [15:0] Seq,
  input  CLK,
  input  I,
  output Output
);

  wire and_1_out, p_out;
  wire [7:0] decoder_1_out7;

  Decoder #(.select(3)) decoder_1 (
    .out0(decoder_1_out7[7]), .out1(decoder_1_out7[6]), .out2(decoder_1_out7[5]), .out3(decoder_1_out7[4]),
    .out4(decoder_1_out7[3]), .out5(decoder_1_out7[2]), .out6(decoder_1_out7[1]), .out7(decoder_1_out7[0]),
    .sel(IR[14:12]));  // open: en
  and p (p_out, decoder_1_out7[0], I, Seq[3]);
  and and_1 (and_1_out, p_out, IR[10]);
  J_K_Flip_Flop j_k_ff_1 (.J(1'b0), .clk(CLK), .K(and_1_out), .Q(Output));  // open: Qn, preset, en, reset

  // Notes on the sheet:
  //   T
  //   B
  //   D
endmodule

module SC_Controller (
  input  [15:0] IR,
  input  [15:0] Seq,
  input  I,
  input  R,
  input  S,
  output LD,
  output INC
);

  wire and_1_out, and_2_out, and_3_out, and_4_out, or_1_out, or_2_out, or_3_out, p_out, r_out;
  wire [7:0] decoder_1_out7;

  Decoder #(.select(3)) decoder_1 (
    .out0(decoder_1_out7[7]), .out1(decoder_1_out7[6]), .out2(decoder_1_out7[5]), .out3(decoder_1_out7[4]),
    .out4(decoder_1_out7[3]), .out5(decoder_1_out7[2]), .out6(decoder_1_out7[1]), .out7(decoder_1_out7[0]),
    .sel(IR[14:12]));  // open: en
  or or_1 (or_1_out, decoder_1_out7[4], decoder_1_out7[3]);
  or or_2 (or_2_out, decoder_1_out7[7], decoder_1_out7[6], decoder_1_out7[5], decoder_1_out7[2]);
  and u_r (r_out, decoder_1_out7[0], Seq[3], ~I);  // AND_Gate
  and and_1 (and_1_out, R, Seq[2]);
  and p (p_out, Seq[3], I, decoder_1_out7[0]);
  and and_2 (and_2_out, decoder_1_out7[1], Seq[6]);
  and and_3 (and_3_out, Seq[4], or_1_out);
  and and_4 (and_4_out, Seq[5], or_2_out);
  or or_3 (or_3_out, r_out, and_1_out, p_out, and_2_out, and_3_out, and_4_out);
  and and_5 (LD, or_3_out, S);
  and and_6 (INC, ~or_3_out, S);  // AND_Gate

  // Notes on the sheet:
  //   T
  //   B
  //   D
endmodule

module SC (
  input  Clear,
  input  Load,
  input  INC,
  input  CLK,
  output A,
  output A_2,
  output A_3,
  output A_4,
  output A_5,
  output A_6,
  output A_7,
  output A_8,
  output C_out
);

  wire and_1_out, and_2_out, and_3_out, and_4_out, and_5_out, and_6_out, and_7_out, and_8_out, and_9_out,
       and_10_out, and_11_out, and_12_out, and_13_out, and_14_out, and_15_out, and_16_out, and_18_out,
       and_19_out, and_21_out, and_22_out, and_24_out, and_25_out, or_1_out, or_2_out, or_3_out, or_4_out,
       or_5_out, or_6_out, or_7_out, or_8_out, or_9_out, or_10_out, or_11_out, or_12_out, or_13_out,
       or_14_out, or_15_out, or_16_out, undriven, undriven_2, undriven_3, undriven_4, undriven_5, undriven_6,
       undriven_7, undriven_8;

  and and_1 (and_1_out, ~Clear, Load);  // AND_Gate
  and and_2 (and_2_out, ~Clear, ~Load, INC);  // AND_Gate
  and and_3 (and_3_out, and_1_out, undriven);
  and and_4 (and_4_out, and_1_out, ~undriven);  // AND_Gate
  and and_5 (and_5_out, and_2_out, A);
  and and_6 (and_6_out, and_1_out, undriven_2);
  and and_7 (and_7_out, and_1_out, ~undriven_2);  // AND_Gate
  and and_8 (and_8_out, and_5_out, A_2);
  and and_9 (and_9_out, and_1_out, undriven_3);
  and and_10 (and_10_out, and_1_out, ~undriven_3);  // AND_Gate
  and and_11 (and_11_out, and_8_out, A_3);
  and and_12 (and_12_out, and_1_out, undriven_4);
  and and_13 (and_13_out, and_1_out, ~undriven_4);  // AND_Gate
  and and_14 (and_14_out, and_11_out, A_4);
  and and_15 (and_15_out, and_1_out, undriven_5);
  and and_16 (and_16_out, and_1_out, ~undriven_5);  // AND_Gate
  and and_17 (Clear, and_14_out, A_5);
  and and_18 (and_18_out, and_1_out, undriven_6);
  and and_19 (and_19_out, and_1_out, ~undriven_6);  // AND_Gate
  and and_20 (Clear, Clear, A_6);
  and and_21 (and_21_out, and_1_out, undriven_7);
  and and_22 (and_22_out, and_1_out, ~undriven_7);  // AND_Gate
  and and_23 (Clear, Clear, A_7);
  and and_24 (and_24_out, and_1_out, undriven_8);
  and and_25 (and_25_out, and_1_out, ~undriven_8);  // AND_Gate
  and and_26 (C_out, Clear, A_8);
  or or_1 (or_1_out, and_2_out, and_3_out);
  or or_2 (or_2_out, Clear, and_2_out, and_4_out);
  or or_3 (or_3_out, and_5_out, and_6_out);
  or or_4 (or_4_out, Clear, and_5_out, and_7_out);
  or or_5 (or_5_out, and_8_out, and_9_out);
  or or_6 (or_6_out, Clear, and_8_out, and_10_out);
  or or_7 (or_7_out, and_11_out, and_12_out);
  or or_8 (or_8_out, Clear, and_11_out, and_13_out);
  or or_9 (or_9_out, and_14_out, and_15_out);
  or or_10 (or_10_out, Clear, and_14_out, and_16_out);
  or or_11 (or_11_out, Clear, and_18_out);
  or or_12 (or_12_out, Clear, Clear, and_19_out);
  or or_13 (or_13_out, Clear, and_21_out);
  or or_14 (or_14_out, Clear, Clear, and_22_out);
  or or_15 (or_15_out, Clear, and_24_out);
  or or_16 (or_16_out, Clear, Clear, and_25_out);
  J_K_Flip_Flop j_k_ff_1 (.J(or_1_out), .clk(CLK), .K(or_2_out), .Q(A));  // open: Qn, preset, en, reset
  J_K_Flip_Flop j_k_ff_2 (.J(or_3_out), .clk(CLK), .K(or_4_out), .Q(A_2));  // open: Qn, preset, en, reset
  J_K_Flip_Flop j_k_ff_3 (.J(or_5_out), .clk(CLK), .K(or_6_out), .Q(A_3));  // open: Qn, preset, en, reset
  J_K_Flip_Flop j_k_ff_4 (.J(or_7_out), .clk(CLK), .K(or_8_out), .Q(A_4));  // open: Qn, preset, en, reset
  J_K_Flip_Flop j_k_ff_5 (.J(or_9_out), .clk(CLK), .K(or_10_out), .Q(A_5));  // open: Qn, preset, en, reset
  J_K_Flip_Flop j_k_ff_6 (.J(or_11_out), .clk(CLK), .K(or_12_out), .Q(A_6));  // open: Qn, preset, en, reset
  J_K_Flip_Flop j_k_ff_7 (.J(or_13_out), .clk(CLK), .K(or_14_out), .Q(A_7));  // open: Qn, preset, en, reset
  J_K_Flip_Flop j_k_ff_8 (.J(or_15_out), .clk(CLK), .K(or_16_out), .Q(A_8));  // open: Qn, preset, en, reset
endmodule
